# Fritzing sketch fritzing (saved by Fritzing 0.9.6b)

parts:
  U1 = LCD-16X2 [package=lcd-16x2_noholes]
  S2 = Pushbutton [part_number="HOUR SET" package="[THT]"]
  S3 = Pushbutton [part_number="MINUTE SET" package="[THT]"]
  S1 = Pushbutton [part_number=RESET package="[THT]"]
  INPUTS = Header 10 [package=1x10-2mm-smd]
  R1 = Resistor [tolerance=±5% power=0.25 resistance=10k package=THT]
  R2 = Resistor [tolerance=±5% power=0.25 resistance=10k package=THT]
  R3 = Resistor [tolerance=±5% power=0.25 resistance=10k package=THT]
  OUTPUTS = Header 10 [package=1x10-2mm-smd]
  R4 = Trimmer Potentiometer [maximum_resistance=10kΩ package=THT]

nets:
  N1: U1.VSS, U1.K, OUTPUTS.9
  N2: U1.VDD, U1.R_W, U1.A, OUTPUTS.10
  N3: U1.VO, R4.wiper
  N4: U1.RS, OUTPUTS.6
  N5: U1.E, OUTPUTS.5
  N6: U1.DB4, OUTPUTS.1
  N7: U1.DB5, OUTPUTS.2
  N8: U1.DB6, OUTPUTS.3
  N9: U1.DB7, OUTPUTS.4
  N10: S2.Pin_1, S2.Pin_2, INPUTS.7, R2.Pin_1
  N11: S2.Pin_3, S2.Pin_4, S3.Pin_3, S3.Pin_4, INPUTS.10, R1.Pin_0
  N12: S3.Pin_1, S3.Pin_2, R3.Pin_1
  N13: S1.Pin_2, R1.Pin_1
  N14: S1.Pin_3, S1.Pin_4, INPUTS.9, R2.Pin_0
